# Fritzing sketch Neuses Shcaltplen des Projekt Fernsteuerung eines Fahrzeug (saved by Fritzing 1.0.2b)
breadboards: 1

parts:
  VCC1 = 4 x AAA Battery Mount
  Buck_Convertor1 = Buck Convertor [part_number=LM2596 package=THT]
  Raspberry_Pi_1 = Raspberry Pi 4 [part_number=RPI-4-b]
  M1 = gear-motor
  J4 = Basic Servo
  Buck_Convertor2 = Buck Convertor [part_number=LM2596 package=THT]
  S1 = H-Bridge with L298N

nets:
  GND: VCC1.-, Buck_Convertor1.Negative_Input, Buck_Convertor1.Negative_Output, Raspberry_Pi_1.GND, J4.gnd, Buck_Convertor2.Negative_Input, Buck_Convertor2.Negative_Output, S1.GND
  N1: VCC1.+, Buck_Convertor1.Positive_Input, Buck_Convertor2.Positive_Input, S1.12V
  N2: Buck_Convertor1.Positive_Output, J4.vcc
  N3: Raspberry_Pi_1.GPIO22, J4.pulse
  N4: Raspberry_Pi_1.GPIO24, S1.IN2
  N5: Raspberry_Pi_1.GPIO23, S1.IN1
  N6: Raspberry_Pi_1.GPIO18, S1.ENA
  N7: Raspberry_Pi_1.5V, Buck_Convertor2.Positive_Output
  N8: M1.pin_1, S1.M1-02
  N9: M1.pin_2, S1.M1-01

notes:
  [Cytron MD30C (ersetzt durch L298N) ]
  [Scheibenwischermotor (12 V Gear Motor)]
  Servomotor braucht eine min. 6V Spannung
  Raspberry Pi braucht eine 5V Spannung
  12V Batterie
  Buckkonverter1 12V In = 6V Out fürden Servo
  Buck-Konverter 2 12V In = 5V Out für den Pi

custom parts:
  Buck Convertor: DC to DC buck convertor
  Raspberry Pi 4: The RPi4, a faster version of the awesome Raspberry Pi 2 B ARM Board with 40 pin gpio. Ready for special Raspberry Pi B+ and RPi2 Hat (Hardware attached (on) top)
  H-Bridge with L298N: h-bridge

// code stored in the sketch: Untitled.ino
import RPi.GPIO as GPIO
import time



GPIO.setmode(GPIO.BCM)


TRIG = 23
ECHO = 24
LED1 = 13
LED2 = 19
buzzer = 26
motor1a= 3
motor1b= 4
motor2a= 20
motor2b= 21
motor= 25
i=0


GPIO.setup(TRIG,GPIO.OUT)
GPIO.setup(ECHO,GPIO.IN)


GPIO.setup(LED1,GPIO.OUT)
GPIO.setup(LED2,GPIO.OUT)
GPIO.setup(buzzer,GPIO.OUT)
GPIO.setup(motor1a,GPIO.OUT)
GPIO.setup(motor1b,GPIO.OUT)
GPIO.setup(motor2a,GPIO.OUT)
GPIO.setup(motor2b,GPIO.OUT)
GPIO.setup(motor,GPIO.OUT)






GPIO.output(TRIG, False)
print("Calibrating.....")
print("Place the object......")




while True:
    GPIO.output(TRIG, True)
    time.sleep(0.00001)
    GPIO.output(TRIG, False)


    while GPIO.input(ECHO)==0:
        pulse_start = time.time()


    while GPIO.input(ECHO)==1:
        pulse_end = time.time()


    pulse_duration = pulse_end - pulse_start


    distance = pulse_duration * 17150


    distance = round(distance+1.15, 2)
  
    if distance<=10:
        print("distance:",distance,"cm")
        GPIO.output(LED1,GPIO.HIGH)
        GPIO.output(LED2,GPIO.LOW)
        GPIO.output(buzzer,GPIO.HIGH)
        GPIO.output(motor1a,GPIO.HIGH)
        GPIO.output(motor1b,GPIO.LOW)
        GPIO.output(motor2a,GPIO.HIGH)
        GPIO.output(motor2b,GPIO.LOW)
        GPIO.output(motor,GPIO.HIGH)
        time.sleep(1)
        GPIO.output(buzzer,GPIO.LOW)
        
    else:
        print("place the object....")
        GPIO.output(LED1,GPIO.LOW)
        GPIO.output(LED2,GPIO.HIGH)
        GPIO.output(buzzer,GPIO.LOW)
        GPIO.output(motor1a,GPIO.LOW)
        GPIO.output(motor1b,GPIO.HIGH)
        GPIO.output(motor2a,GPIO.LOW)
        GPIO.output(motor2b,GPIO.HIGH)
        GPIO.output(motor,GPIO.HIGH)
